# Fritzing sketch CANProject (saved by Fritzing 0.9.10b)
breadboards: 2

parts:
  Componente1 = Arduino Uno (Rev3)
  RHT1 = Humidity and Temperature Sensor RHT03
  M1 = Niren can bus module [package=THT]
  Componente3 = Arduino Uno (Rev3)
  M3 = Niren can bus module [package=THT]
  Componente4 = Arduino Uno (Rev3)
  RHT2 = Humidity and Temperature Sensor RHT03
  M4 = Niren can bus module [package=THT]
  Componente5 = Arduino Uno (Rev3)
  M5 = Niren can bus module [package=THT]
  Componente6 = LCD1602-I2C

nets:
  N1: Componente1.A0, RHT1.Data-signal
  N2: Componente1.D10_PWM/SS, M1.pin3
  N3: Componente1.D11_PWM/MOSI, M1.pin5
  N4: Componente1.D12/MISO, M1.pin4
  N5: Componente1.D13/SCK, M1.pin6
  N6: Componente1.GND, RHT1.GND_2, M1.pin2
  5V: Componente1.5V, RHT1.Vcc, M1.pin1
  N7: M1.pin10, M1.pin12, M3.pin10, M4.pin10, M4.pin12
  N8: M1.pin11, M1.pin13, M3.pin11, M4.pin11, M4.pin13
  N9: Componente3.D10_PWM/SS, M3.pin3
  N10: Componente3.D11_PWM/MOSI, M3.pin5
  N11: Componente3.D12/MISO, M3.pin4
  N12: Componente3.D13/SCK, M3.pin6
  N13: Componente3.5V, M3.pin1
  N14: Componente3.GND, M3.pin2
  N15: Componente4.A0, RHT2.Data-signal
  N16: Componente4.D10_PWM/SS, M4.pin3
  N17: Componente4.D11_PWM/MOSI, M4.pin5
  N18: Componente4.D12/MISO, M4.pin4
  N19: Componente4.D13/SCK, M4.pin6
  N20: Componente4.GND, RHT2.GND_2, M4.pin2
  5V_2: Componente4.5V, RHT2.Vcc, M4.pin1
  N21: Componente5.A4/SDA, Componente6.SDA
  N22: Componente5.A5/SCL, Componente6.SCL
  N23: Componente5.D10_PWM/SS, M5.pin3
  N24: Componente5.D11_PWM/MOSI, M5.pin5
  N25: Componente5.D12/MISO, M5.pin4
  N26: Componente5.D13/SCK, M5.pin6
  5V_3: Componente5.5V, M5.pin1, Componente6.VCC
  GND: Componente5.GND, M5.pin2, Componente6.GND

custom parts:
  Niren can bus module: Niren can bus module availabe on ebay and others. Pcb view assumes that you unsolder the 7 pin header and resolder it on the bottom of the module to connect to the pcb. The two jumpers and the can bus connector remain on the top of the board and don't appear in pcb view.
  LCD1602-I2C: A standard character display, usually with 2x16 characters. Comes in many colors with LCM1602 IIC attached.
